# Fritzing sketch Thermo Webserver (saved by Fritzing 0.7.7b)

parts:
  U1 = Arduino Mega
  Arduino_Ethernet_Shield1 = Arduino Ethernet Shield
  LCD_Shield = LCD screen
  Firebox = MAX31855 Breakout Board with Thermocouple
  Chimney = MAX31855 Breakout Board with Thermocouple
  Water_Tank = MAX31855 Breakout Board with Thermocouple
  Oven = MAX31855 Breakout Board with Thermocouple
  TMP36_Analog_Temperature_Sensor = mystery part, 3 pins [chip_label=TMP36]

nets:
  N1: U1.D5, Firebox.CLK
  N2: U1.D3, Firebox.DO
  N3: U1.+5V, LCD_Shield.LED+
  N4: U1.GND, LCD_Shield.LED-, TMP36_Analog_Temperature_Sensor.pin3
  N5: U1.D16, Firebox.CS
  N6: U1.D17, Chimney.CS
  N7: U1.D20, LCD_Shield.DB6
  N8: U1.D21, LCD_Shield.DB7
  N9: U1.D22, Water_Tank.CS
  N10: U1.D24, Oven.CS
  N11: Arduino_Ethernet_Shield1.aref, TMP36_Analog_Temperature_Sensor.pin1
  N12: Arduino_Ethernet_Shield1.3V3, Firebox.3Vo
  N13: Arduino_Ethernet_Shield1.GND#19, Firebox.GND
  N14: Arduino_Ethernet_Shield1.A0, TMP36_Analog_Temperature_Sensor.pin2

notes:
  PowerSwitch Tail II
